# Fritzing sketch tlc (saved by Fritzing 0.9.3b)
circuit board: 10.1278cm x 6.96452cm
breadboards: 1

parts:
  Componente1 = Arduino Nano (Rev3.0)
  U1 = Packages: [package=dil28-3]
  Power_plug1 = Power plug
  C1 = Electrolytic Capacitor [capacitance=1µF package="100 mil [THT, electrolytic]"]
  C2 = Ceramic Capacitor [capacitance=100nF package="100 mil [THT, multilayer]"]
  R1 = Resistor [tolerance=±5% resistance=2.2k package="1206 [SMD]"]

nets:
  N1: Componente1.D3, U1.GSCLK
  N2: Componente1.D9, U1.XLAT
  N3: Componente1.D10, U1.BLANK
  N4: Componente1.D11/MOSI, U1.SIN
  N5: Componente1.D13/SCK, U1.SCLK
  VCC: U1.DCPRG, U1.VCC, Power_plug1.VCC, C1.-, C2.0
  GND: U1.IREF, U1.GND, U1.VPRG, Power_plug1.GND, C1.+, C2.1, R1.Pin_0, R1.Pin_1
